# Fritzing sketch esquema_1 (saved by Fritzing 1.0.3b)
breadboards: 1

parts:
  Raspberry_Pi_1 = Raspberry Pi 3 [part_number=RPI-3-V1.2]
  R1 = Resistor [tolerance=±5% resistance=220 package="2512 [SMD]"]
  R2 = Resistor [tolerance=±5% resistance=220 package="2512 [SMD]"]
  LED1 = smd LED [color="Red (633nm)" package="0805 [SMD]"]
  LED2 = smd LED [color="Red (633nm)" package="0805 [SMD]"]

nets:
  N1: Raspberry_Pi_1.GPIO17, R1.Pin_1
  N2: Raspberry_Pi_1.GND, LED1.cathode, LED2.cathode
  N3: Raspberry_Pi_1.GPIO25, R2.Pin_1
  N4: R1.Pin_0, LED1.anode
  N5: R2.Pin_0, LED2.anode
