# Fritzing sketch esquema_2 (saved by Fritzing 1.0.3b)
breadboards: 1

parts:
  R1 = Resistor [tolerance=±5% resistance=220 package="2512 [SMD]"]
  R2 = Resistor [tolerance=±5% resistance=220 package="2512 [SMD]"]
  LED1 = smd LED [color="Red (633nm)" package="0805 [SMD]"]
  LED2 = smd LED [color="Red (633nm)" package="0805 [SMD]"]
  R3 = Resistor [tolerance=±5% power=0.25W resistance=220 package=THT]
  LED3 = smd LED [color="Red (633nm)" package="0805 [SMD]"]
  Raspberry_Pi_1 = Raspberry Pi 3 [part_number=RPI-3-V1.2]
  HC-SR04_Sensor_1 = HC-SR04 Ultrasonic Distance Sensor

nets:
  N1: R1.Pin_0, LED1.anode
  N2: R1.Pin_1, Raspberry_Pi_1.GPIO13
  N3: R2.Pin_0, LED2.anode
  N4: R2.Pin_1, Raspberry_Pi_1.GPIO16
  GND: LED1.cathode, LED2.cathode, LED3.cathode, Raspberry_Pi_1.GND, HC-SR04_Sensor_1.GND
  N5: R3.Pin_0, LED3.anode
  N6: R3.Pin_1, Raspberry_Pi_1.GPIO12
  N7: Raspberry_Pi_1.GPIO17, HC-SR04_Sensor_1.TRIG
  N8: Raspberry_Pi_1.GPIO25, HC-SR04_Sensor_1.ECHO
  5V: Raspberry_Pi_1.5V, HC-SR04_Sensor_1.VCC
