# Fritzing sketch esquema_4 (saved by Fritzing 1.0.3b)
breadboards: 1

parts:
  Raspberry_Pi_1 = Raspberry Pi 3 [part_number=RPI-3-V1.2]
  U2 = LCD-16X2 [package=lcd-16x2]
  U3 = POT [knob_status=50% power=0.5W package=pot_alpha_rv16af-20]
  HC-SR04_Sensor_1 = HC-SR04 Ultrasonic Distance Sensor

nets:
  N1: Raspberry_Pi_1.GPIO4, U2.RS
  N2: Raspberry_Pi_1.GPIO17, HC-SR04_Sensor_1.TRIG
  N3: Raspberry_Pi_1.GPIO27, U2.DB4
  N4: Raspberry_Pi_1.GPIO22, U2.DB5
  GND: Raspberry_Pi_1.GND, U2.VSS, U2.R_W, U2.K, HC-SR04_Sensor_1.GND
  N5: Raspberry_Pi_1.GPIO25, HC-SR04_Sensor_1.ECHO
  N6: Raspberry_Pi_1.GPIO24, U2.DB7
  N7: Raspberry_Pi_1.GPIO23, U2.DB6
  N8: Raspberry_Pi_1.GPIO18, U2.E
  5V: Raspberry_Pi_1.5V, U2.VDD, U2.A, U3.E, HC-SR04_Sensor_1.VCC
  N9: U2.VO, U3.S
